// Digital circuit hazard-unit.dig as structural Verilog
module hazard_unit (
  input  [4:0] RR0_2,
  input  [4:0] WR_4,
  input  [4:0] WR_3,
  input  [4:0] RR1_2,
  input  RFW_4,
  input  RFW_3,
  input  PCBr_2,
  input  MR_3,
  input  CLR,
  output [1:0] FRD0_sel,
  output [1:0] FRD1_sel,
  output flush_0,
  output flush_1,
  output Stall_0,
  output Stall_1,
  output flush_2,
  output Stall_2
);

  wire and_2_out, and_3_out, and_4_out, and_5_out, comparator_1_eq, comparator_3_eq, or_1_out, RR0_hazard,
       RR1_hazard;

  or or_1 (or_1_out, RR0_hazard, RR1_hazard);
  Comparator #(.Bits(5)) comparator_1 (.a(RR0_2), .b(WR_4), .eq(comparator_1_eq));  // open: gt, lt
  Comparator #(.Bits(5)) comparator_2 (.a(RR0_2), .b(WR_3), .eq(RR0_hazard));  // open: gt, lt
  Comparator #(.Bits(5)) comparator_3 (.a(RR1_2), .b(WR_4), .eq(comparator_3_eq));  // open: gt, lt
  Comparator #(.Bits(5)) comparator_4 (.a(RR1_2), .b(WR_3), .eq(RR1_hazard));  // open: gt, lt
  or or_2 (flush_0, PCBr_2, CLR);
  and and_1 (flush_2, MR_3, or_1_out);
  and and_2 (and_2_out, RFW_4, comparator_1_eq);
  and and_3 (and_3_out, RFW_3, RR0_hazard);
  and and_4 (and_4_out, RFW_4, comparator_3_eq);
  and and_5 (and_5_out, RFW_3, RR1_hazard);
  not not_1 (Stall_0, flush_2);
  PriorityEncoder #(.Selector_Bits(2)) priorityencoder_1 (
    .in0(1'b1), .in1(and_2_out), .in2(and_3_out), .in3(1'b0), .num(FRD0_sel));  // open: any
  PriorityEncoder #(.Selector_Bits(2)) priorityencoder_2 (
    .in0(1'b1), .in1(and_4_out), .in2(and_5_out), .in3(1'b0), .num(FRD1_sel));  // open: any

  assign flush_1 = flush_0;
  assign Stall_1 = Stall_0;
  assign Stall_2 = Stall_0;
endmodule
